# Fritzing sketch Breadboard_Circuit (saved by Fritzing 0.9.9b)
breadboards: 1

parts:
  U1 = Mini-360 DC-DC Buck converter [package=THT]
  Part1 = Arduino Nano (Rev3.0)
  Q1 = npn-Powertransistor [package="TO220 [THT]"]
  R1 = Resistor [tolerance=±5% resistance=220 package=THT]
  J3 = Screw terminal - 2 pins [package=THT]
  J4 = Screw terminal - 2 pins [package=THT]
  R2 = Resistor [tolerance=±5% resistance=220 package="0603 [SMD]"]

nets:
  N1: U1.IN-, U1.OUT-, Part1.GND, Q1.emitter, R1.Pin_1, J3.pin1
  N2: U1.IN+, J3.pin2, J4.pin2
  N3: U1.OUT+, Part1.VIN
  N4: Part1.D8, R2.Pin_1
  N5: Q1.base, R1.Pin_0, R2.Pin_0
  N6: Q1.collector, J4.pin1

notes:
  12V DC Power Supply
  To EL inverter

custom parts:
  Mini-360 DC-DC Buck converter: Mini-360 DC-DC Buck converter. Tiny buck step down voltage converter, input voltage 4.75 to 23V output 1 to 17V adjustable. Available from ebay and the like.
